// Logisim project experiment.circ as structural Verilog
module \抢答判别模块  (
  input  START,
  input  RESET,
  input  K0,
  input  K1,
  input  K2,
  input  K3,
  output Q0,
  output Q1,
  output Q2,
  output Q3,
  output ALLOW,
  output LOCK,
  output ENABLE
);

  wire and_1_out, and_2_out, and_3_out, and_4_out, clock_1_out, not_1_out, not_2_out, not_3_out, or_2_out;

  Clock clock_1 (.out(clock_1_out));
  S_R_Flip_Flop s_r_ff_1 (.S(START), .clk(clock_1_out), .R(or_2_out), .Q(ALLOW));  // open: Qn, preset, reset
  not not_1 (not_1_out, K0);
  S_R_Flip_Flop u_Q0 (.S(and_1_out), .clk(clock_1_out), .R(RESET), .Q(Q0));  // open: Qn, preset, reset
  and and_1 (and_1_out, ENABLE, K0);
  S_R_Flip_Flop u_Q1 (.S(and_2_out), .clk(clock_1_out), .R(RESET), .Q(Q1));  // open: Qn, preset, reset
  and and_2 (and_2_out, ENABLE, K1, not_1_out);
  not not_2 (not_2_out, K1);
  and and_3 (and_3_out, ENABLE, K2, not_1_out, not_2_out);
  not not_3 (not_3_out, K2);
  S_R_Flip_Flop u_Q2 (.S(and_3_out), .clk(clock_1_out), .R(RESET), .Q(Q2));  // open: Qn, preset, reset
  S_R_Flip_Flop u_Q3 (.S(and_4_out), .clk(clock_1_out), .R(RESET), .Q(Q3));  // open: Qn, preset, reset
  and and_4 (and_4_out, ENABLE, K3, not_1_out, not_2_out, not_3_out);
  or or_1 (LOCK, Q0, Q1, Q2, Q3);
  or or_2 (or_2_out, RESET, LOCK);
  and and_5 (ENABLE, ALLOW, ~LOCK);  // AND_Gate

  // Notes on the sheet:
  //   K0: pull=down
  //   K3: pull=down
  //   START: pull=down
  //   K2: pull=down
  //   RESET: pull=down
  //   K1: pull=down
endmodule

module \计时器  (
  input  BEEP_CLK,
  input  [1:0] TIME_SEL,
  input  SEC_CLK,
  input  TIMER_START,
  input  RESET,
  output TIME_UP,
  output TIME_ALARM,
  output [3:0] COUNT_ONES,
  output [3:0] COUNT_TENS,
  output TIMER_LED,
  output RUN
);

  wire buzzer_1_p2, clock_1_out, comparator_1_eq, comparator_2_eq, COUNT_CLK_out, COUNT_ONES_tc, not_1_out,
       not_2_out, or_1_out, or_2_out;
  wire [3:0] multiplexer_1_out;

  Comparator #(.width(4), .mode("unsigned")) comparator_1 (
    .a(COUNT_TENS), .b(multiplexer_1_out), .eq(comparator_1_eq));  // open: gt, lt
  Multiplexer #(.select(2), .width(4), .enable("false")) multiplexer_1 (
    .in0(4'b0001), .in1(4'b0010), .in2(4'b0101), .in3(4'b0110), .out(multiplexer_1_out), .sel(TIME_SEL));
  Comparator #(.width(4), .mode("unsigned")) comparator_2 (
    .a(COUNT_ONES), .b(4'b0000), .eq(comparator_2_eq));  // open: gt, lt
  not not_1 (not_1_out, or_1_out);
  or or_1 (or_1_out, RESET, TIMER_START);
  Clock clock_1 (.out(clock_1_out));
  or or_2 (or_2_out, RESET, TIME_UP);
  and u_TIME_UP (TIME_UP, RUN, comparator_2_eq, comparator_1_eq);
  _74160 u_COUNT_ONES (
    .CLK(COUNT_CLK_out), .CLR(not_1_out), .LE(1'b1), .CEP(1'b1), .CET(1'b1), .Q1(COUNT_ONES[0]),
    .Q2(COUNT_ONES[1]), .Q3(COUNT_ONES[2]), .Q4(COUNT_ONES[3]), .TC(COUNT_ONES_tc));  // open: D1, D2, D3, D4
  and COUNT_CLK (COUNT_CLK_out, RUN, SEC_CLK);
  S_R_Flip_Flop s_r_ff_1 (.S(TIMER_START), .clk(clock_1_out), .R(or_2_out), .Q(RUN));  // open: Qn, preset, reset
  LED led_1 (.in(TIME_ALARM));
  S_R_Flip_Flop s_r_ff_2 (.S(TIME_UP), .clk(clock_1_out), .R(or_1_out), .Q(TIME_ALARM));  // open: Qn, preset, reset
  not not_2 (not_2_out, COUNT_ONES_tc);
  // Buzzer buzzer_1: pin names not known; wires that end beside it: 12'h999, buzzer_1_p2, {7{1'b1}}
  and and_1 (buzzer_1_p2, BEEP_CLK, TIME_ALARM);
  _74160 u_COUNT_TENS (
    .CLK(not_2_out), .CLR(not_1_out), .LE(1'b1), .CEP(1'b1), .CET(1'b1), .Q1(COUNT_TENS[0]),
    .Q2(COUNT_TENS[1]), .Q3(COUNT_TENS[2]), .Q4(COUNT_TENS[3]));  // open: D1, D2, D3, D4, TC

  assign TIMER_LED = RUN;

  // Notes on the sheet:
  //   TIMER_START: pull=down
  //   RESET: pull=down
endmodule

module _74160 (
  input  CLK,
  input  CLR,
  input  LE,
  input  CEP,
  input  CET,
  input  D1,
  input  D2,
  input  D3,
  input  D4,
  output Q1,
  output Q2,
  output Q3,
  output Q4,
  output TC
);

  wire and_1_out, and_2_out, and_3_out, and_4_out, and_5_out, and_6_out, and_7_out, and_8_out, and_9_out,
       and_10_out, and_11_out, and_12_out, and_13_out, d_ff_4_qn, not_1_out, not_2_out, or_1_out, or_2_out,
       or_3_out, or_4_out, or_5_out, xor_1_out, xor_2_out, xor_3_out, xor_4_out;

  not not_1 (not_1_out, CLR);
  and and_1 (and_1_out, LE, CEP, CET);
  not not_2 (not_2_out, LE);
  and and_2 (and_2_out, D1, not_2_out);
  and and_3 (and_3_out, Q1, LE);
  and and_4 (and_4_out, D2, not_2_out);
  and and_5 (and_5_out, Q2, LE);
  and and_6 (and_6_out, Q1, and_1_out, d_ff_4_qn);
  and and_7 (and_7_out, D3, not_2_out);
  and and_8 (and_8_out, Q3, LE);
  and and_9 (and_9_out, Q2, Q1, and_1_out);
  and and_10 (and_10_out, D4, not_2_out);
  and and_11 (and_11_out, Q4, LE);
  and and_12 (and_12_out, Q3, Q2, Q1, and_1_out);
  and and_13 (and_13_out, Q4, Q1, and_1_out);
  xor xor_1 (xor_1_out, and_3_out, and_1_out);
  xor xor_2 (xor_2_out, and_5_out, and_6_out);
  xor xor_3 (xor_3_out, and_8_out, and_9_out);
  or or_1 (or_1_out, and_12_out, and_13_out);
  or or_2 (or_2_out, and_2_out, xor_1_out);
  or or_3 (or_3_out, and_4_out, xor_2_out);
  or or_4 (or_4_out, and_7_out, xor_3_out);
  or or_5 (or_5_out, and_10_out, xor_4_out);
  xor xor_4 (xor_4_out, and_11_out, or_1_out);
  D_Flip_Flop d_ff_1 (.clk(CLK), .D(or_2_out), .Q(Q1), .reset(not_1_out));  // open: Qn, preset
  D_Flip_Flop d_ff_2 (.clk(CLK), .D(or_3_out), .Q(Q2), .reset(not_1_out));  // open: Qn, preset
  D_Flip_Flop d_ff_3 (.clk(CLK), .D(or_4_out), .Q(Q3), .reset(not_1_out));  // open: Qn, preset
  D_Flip_Flop d_ff_4 (.clk(CLK), .D(or_5_out), .Q(Q4), .Qn(d_ff_4_qn), .reset(not_1_out));  // open: preset
  and and_14 (TC, Q4, Q1, CET);
endmodule

module _74161 (
  input  CLK,
  input  CLR,
  input  LE,
  input  CEP,
  input  CET,
  input  D1,
  input  D2,
  input  D3,
  input  D4,
  output Q1,
  output Q2,
  output Q3,
  output Q4,
  output TC
);

  wire and_1_out, and_2_out, and_3_out, and_4_out, and_5_out, and_6_out, and_7_out, and_8_out, and_9_out,
       and_10_out, and_11_out, and_12_out, not_1_out, not_2_out, or_1_out, or_2_out, or_3_out, or_4_out,
       xor_1_out, xor_2_out, xor_3_out, xor_4_out;

  not not_1 (not_1_out, CLR);
  and and_1 (and_1_out, LE, CEP, CET);
  not not_2 (not_2_out, LE);
  and and_2 (and_2_out, D1, not_2_out);
  and and_3 (and_3_out, Q1, LE);
  and and_4 (and_4_out, D2, not_2_out);
  and and_5 (and_5_out, Q2, LE);
  and and_6 (and_6_out, Q1, and_1_out);
  and and_7 (and_7_out, D3, not_2_out);
  and and_8 (and_8_out, Q3, LE);
  and and_9 (and_9_out, Q2, Q1, and_1_out);
  and and_10 (and_10_out, D4, not_2_out);
  and and_11 (and_11_out, Q4, LE);
  and and_12 (and_12_out, Q3, Q2, Q1, and_1_out);
  xor xor_1 (xor_1_out, and_3_out, and_1_out);
  xor xor_2 (xor_2_out, and_5_out, and_6_out);
  xor xor_3 (xor_3_out, and_8_out, and_9_out);
  xor xor_4 (xor_4_out, and_11_out, and_12_out);
  or or_1 (or_1_out, and_2_out, xor_1_out);
  or or_2 (or_2_out, and_4_out, xor_2_out);
  or or_3 (or_3_out, and_7_out, xor_3_out);
  or or_4 (or_4_out, and_10_out, xor_4_out);
  D_Flip_Flop d_ff_1 (.clk(CLK), .D(or_1_out), .Q(Q1), .reset(not_1_out));  // open: Qn, preset
  D_Flip_Flop d_ff_2 (.clk(CLK), .D(or_2_out), .Q(Q2), .reset(not_1_out));  // open: Qn, preset
  D_Flip_Flop d_ff_3 (.clk(CLK), .D(or_3_out), .Q(Q3), .reset(not_1_out));  // open: Qn, preset
  D_Flip_Flop d_ff_4 (.clk(CLK), .D(or_4_out), .Q(Q4), .reset(not_1_out));  // open: Qn, preset
  and and_13 (TC, Q4, Q3, Q2, Q1, CET);
endmodule

module \_7_段译码器  (
  input  A0,
  input  A1,
  input  A2,
  input  A3,
  output a,
  output b,
  output c,
  output d,
  output e,
  output f,
  output g
);

  // DisplayDecoder displaydecoder_1: pin names not known; wires that end beside it: {A3, A2, A1, A0}, a, b, c, d, e, f, g
endmodule

// HEX2BCD
module \HEX2BCD_60_以内  (
  input  D0,
  input  D1,
  input  D2,
  input  D3,
  input  D4,
  input  D5,
  input  D6,
  input  D7,
  output D0_2,
  output D1_2,
  output D2_2,
  output D3_2,
  output D4_2,
  output D5_2,
  output D6_2,
  output D7_2
);

  wire adder_1_cout, adder_2_cout, adder_3_cout, adder_4_cout, comparator_1_gt, comparator_2_gt,
       comparator_4_gt, comparator_5_gt, not_1_out, not_2_out;
  wire [2:0] and_1_out;
  wire [7:0] adder_1_out, adder_2_out, adder_3_out, adder_4_out, adder_5_out;

  Adder adder_1 (.a({D7, D6, D5, D4, D3, D2, D1, D0}), .b(8'h6), .out(adder_1_out), .cout(adder_1_cout));  // open: cin
  Adder adder_2 (
    .a({D7, D6, D5, D4, D3, D2, D1, D0}), .b(8'hc), .out(adder_2_out), .cin(adder_1_cout), .cout(adder_2_cout));
  Adder adder_3 (
    .a({D7, D6, D5, D4, D3, D2, D1, D0}), .b(8'h12), .out(adder_3_out), .cin(adder_2_cout),
    .cout(adder_3_cout));
  Adder adder_4 (
    .a({D7, D6, D5, D4, D3, D2, D1, D0}), .b(8'h18), .out(adder_4_out), .cin(adder_3_cout),
    .cout(adder_4_cout));
  Adder adder_5 (.a({D7, D6, D5, D4, D3, D2, D1, D0}), .b(8'h1e), .out(adder_5_out), .cin(adder_4_cout));  // open: cout
  Comparator comparator_1 (.a({D7, D6, D5, D4, D3, D2, D1, D0}), .b(8'h9), .gt(comparator_1_gt));  // open: eq, lt
  Comparator comparator_2 (.a({D7, D6, D5, D4, D3, D2, D1, D0}), .b(8'h13), .gt(comparator_2_gt));  // open: eq, lt
  Comparator comparator_3 (.a({D7, D6, D5, D4, D3, D2, D1, D0}), .b(8'h1d), .gt(and_1_out[2]));  // open: eq, lt
  not not_1 (not_1_out, comparator_4_gt);
  Comparator comparator_4 (.a({D7, D6, D5, D4, D3, D2, D1, D0}), .b(8'h27), .gt(comparator_4_gt));  // open: eq, lt
  not not_2 (not_2_out, comparator_5_gt);
  Comparator comparator_5 (.a({D7, D6, D5, D4, D3, D2, D1, D0}), .b(8'h31), .gt(comparator_5_gt));  // open: eq, lt
  Multiplexer #(.select(3), .width(8), .disabled(0), .enable("false")) multiplexer_1 (
    .in0({D7, D6, D5, D4, D3, D2, D1, D0}), .in1(adder_1_out), .in3(adder_2_out), .in4(adder_5_out),
    .in6(adder_4_out), .in7(adder_3_out), .out({D7_2, D6_2, D5_2, D4_2, D3_2, D2_2, D1_2, D0_2}),
    .sel(and_1_out));  // open: in2, in5
  and and_1 (and_1_out[0], comparator_1_gt, not_1_out);
  and and_2 (and_1_out[1], comparator_2_gt, not_2_out);
endmodule
